// Logisim project CO-assignment.circ as structural Verilog
module NAND_OR (
  input  A,
  input  B,
  output X
);

  wire A_prime_out, B_prime_out;

  not A_prime (A_prime_out, A);  // NAND_Gate
  not B_prime (B_prime_out, B);  // NAND_Gate
  nand A_B (X, A_prime_out, B_prime_out);
endmodule

module NAND_AND (
  input  A,
  input  B,
  output out_3
);

  wire AB__prime_out;

  nand AB__prime (AB__prime_out, A, B);
  not AB (out_3, AB__prime_out);  // NAND_Gate
endmodule

module NAND_NOT (
  input  A,
  output X
);

  not A_prime (X, A);  // NAND_Gate
endmodule

module NAND_NOR (
  input  A,
  input  B,
  output X
);

  wire A_B_out, A_prime_out, B_prime_out;

  not A_prime (A_prime_out, A);  // NAND_Gate
  not B_prime (B_prime_out, B);  // NAND_Gate
  nand A_B (A_B_out, A_prime_out, B_prime_out);
  not A_prime_B_prime (X, A_B_out);  // NAND_Gate
endmodule

module NAND_XOR (
  input  A,
  input  B,
  output X
);

  wire A_B_prime_out, A_prime_B_out, A_prime_out, B_prime_out;

  not A_prime (A_prime_out, A);  // NAND_Gate
  not B_prime (B_prime_out, B);  // NAND_Gate
  nand A_prime_B (A_prime_B_out, A_prime_out, B);
  nand A_B_prime (A_B_prime_out, A, B_prime_out);
  nand A_prime_B_AB_prime (X, A_prime_B_out, A_B_prime_out);
endmodule

module NAND_XNOR (
  input  A,
  input  B,
  output X
);

  wire A_prime_B_out, A_prime_out, AB_prime_out, B_prime_out, nand_1_out;

  not A_prime (A_prime_out, A);  // NAND_Gate
  not B_prime (B_prime_out, B);  // NAND_Gate
  nand A_prime_B (A_prime_B_out, A_prime_out, B);
  nand AB_prime (AB_prime_out, A, B_prime_out);
  nand nand_1 (nand_1_out, A_prime_B_out, AB_prime_out);
  not nand_2 (X, nand_1_out);  // NAND_Gate

  // Notes on the sheet:
  //   (AB')+(A'B)
  //   (A+B')(A'+B)
endmodule

module NOR_OR (
  input  A,
  input  B,
  output X
);

  wire A_prime_B_prime_out;

  nor A_prime_B_prime (A_prime_B_prime_out, A, B);
  not A_B (X, A_prime_B_prime_out);  // NOR_Gate
endmodule

module NOR_AND (
  input  A,
  input  B,
  output X
);

  wire A_prime_out, B_prime_out;

  not A_prime (A_prime_out, A);  // NOR_Gate
  not B_prime (B_prime_out, B);  // NOR_Gate
  nor A_prime_B_prime__prime (X, A_prime_out, B_prime_out);
endmodule

module NOR_NOT (
  input  A,
  output X
);

  not A_prime (X, A);  // NOR_Gate
endmodule

module NOR_NAND (
  input  A,
  input  B,
  output X
);

  wire A_prime_B_prime__prime_out, A_prime_out, B_prime_out;

  not A_prime (A_prime_out, A);  // NOR_Gate
  not B_prime (B_prime_out, B);  // NOR_Gate
  nor A_prime_B_prime__prime (A_prime_B_prime__prime_out, A_prime_out, B_prime_out);
  not AB__prime (X, A_prime_B_prime__prime_out);  // NOR_Gate
endmodule

module NOR_XOR (
  input  A,
  input  B,
  output X
);

  wire A_out, A_prime_2_out, A_prime_3_out, A_prime_B__prime_out, A_prime_out, AB_prime__prime_out, B_out,
       B_prime_out, nor_1_out;

  not u_A (A_out, A_prime_out);  // NOR_Gate
  not A_prime (A_prime_out, A);  // NOR_Gate
  not B_prime (B_prime_out, B);  // NOR_Gate
  not A_prime_2 (A_prime_2_out, A);  // NOR_Gate
  not A_prime_3 (A_prime_3_out, B);  // NOR_Gate
  not u_B (B_out, A_prime_3_out);  // NOR_Gate
  nor AB_prime__prime (AB_prime__prime_out, A_out, B_prime_out);
  nor nor_1 (nor_1_out, AB_prime__prime_out, A_prime_B__prime_out);
  nor A_prime_B__prime (A_prime_B__prime_out, A_prime_2_out, B_out);
  not A_prime_B_AB_prime (X, nor_1_out);  // NOR_Gate

  // Notes on the sheet:
  //   (A+B')(A'+B)
endmodule

module NOR_XNOR (
  input  A,
  input  B,
  output X
);

  wire A_B_prime__prime_out, A_out, A_prime_2_out, A_prime_B__prime_out, A_prime_out, B_out, B_prime_2_out,
       B_prime_out;

  not A_prime (A_prime_out, A);  // NOR_Gate
  not B_prime (B_prime_out, B);  // NOR_Gate
  not u_A (A_out, A_prime_out);  // NOR_Gate
  not B_prime_2 (B_prime_2_out, B);  // NOR_Gate
  not A_prime_2 (A_prime_2_out, A);  // NOR_Gate
  not u_B (B_out, B_prime_out);  // NOR_Gate
  nor A_B_prime__prime (A_B_prime__prime_out, A_out, B_prime_2_out);
  nor A_prime_B__prime (A_prime_B__prime_out, A_prime_2_out, B_out);
  nor nor_1 (X, A_B_prime__prime_out, A_prime_B__prime_out);

  // Notes on the sheet:
  //   AB+A'B'
endmodule

module HalfAdder (
  input  A,
  input  B,
  output Sum,
  output Carry
);

  xor xor_1 (Sum, A, B);
  and and_1 (Carry, A, B);
endmodule

module FullAdder (
  input  A,
  input  B,
  input  Cin,
  output Sum,
  output Carry
);

  wire AB_out, and_1_out, xor_2_out;

  ExactlyOne xor_1 (.out(Sum), .in0(A), .in1(B), .in2(Cin));
  and AB (AB_out, A, B);
  xor xor_2 (xor_2_out, A, B);
  and and_1 (and_1_out, Cin, xor_2_out);
  or or_1 (Carry, AB_out, and_1_out);

  // Notes on the sheet:
  //   A xor B xor C
  //   AxorB
  //   (AxorB)C
  //   AB+(AxorB)C
endmodule

module Multiplexer (
  input  X,
  input  Y,
  output out_3
);

  wire I0_out, I1_out, I2_out, I3_out, not_1_out, not_2_out;

  not not_1 (not_1_out, X);
  not not_2 (not_2_out, Y);
  and I0 (I0_out, not_1_out, not_2_out);
  and I1 (I1_out, not_1_out, Y);
  and I2 (I2_out, X, not_2_out);
  and I3 (I3_out, X, Y);
  or _4_1 (out_3, I0_out, I1_out, I2_out, I3_out);

  // Notes on the sheet:
  //   X'Y'I0 + X'YI1 + XY'I2 + XYI3
endmodule

module BCD_XS3 (
  input  A,
  input  B,
  input  C,
  input  D,
  output W,
  output X,
  output Y,
  output Z
);

  wire B_prime_C_out, B_prime_D_out, BC_out, BC_prime_D_prime_out, BD_out, not_1_out, not_2_out;

  and BC (BC_out, B, C);
  and BD (BD_out, B, D);
  not not_1 (not_1_out, B);
  and B_prime_C (B_prime_C_out, not_1_out, C);
  not not_2 (not_2_out, C);
  not not_3 (Z, D);
  or or_1 (W, A, BC_out, BD_out);
  and B_prime_D (B_prime_D_out, not_1_out, D);
  and BC_prime_D_prime (BC_prime_D_prime_out, B, not_2_out, Z);
  or or_2 (X, B_prime_C_out, B_prime_D_out, BC_prime_D_prime_out);
  xnor xnor_1 (Y, C, D);

  // Notes on the sheet:
  //   w=A+BC+BD
  //   Y=C xnor D
  //   Z=D'
  //   x=B'C+B'D+BC'D'
endmodule

module XS3_BCD (
  input  A,
  input  B,
  input  C,
  input  D,
  output W,
  output X,
  output Y,
  output Z
);

  wire AB_out, ACD_out, B_prime_C_prime_out, B_prime_D_prime_out, BCD_out, not_1_out, not_2_out;

  and AB (AB_out, A, B);
  and ACD (ACD_out, A, C, D);
  or or_1 (W, AB_out, ACD_out);
  not not_1 (not_1_out, B);
  and B_prime_C_prime (B_prime_C_prime_out, not_1_out, not_2_out);
  not not_2 (not_2_out, C);
  and BCD (BCD_out, B, C, D);
  not not_3 (Z, D);
  or or_2 (X, B_prime_C_prime_out, B_prime_D_prime_out, BCD_out);
  and B_prime_D_prime (B_prime_D_prime_out, not_1_out, Z);
  xor xor_1 (Y, C, D);

  // Notes on the sheet:
  //   W=AB+ACD
  //   X=B'C'+B'D'+BCD
  //   Y=C xor D
  //   Z=D'
endmodule

module Gray_Binary (
  input  A,
  input  B,
  input  C,
  input  D,
  output W,
  output X,
  output Y,
  output Z
);

  xor xor_1 (X, A, B);
  xor xor_2 (Y, X, C);
  xor xor_3 (Z, Y, D);

  assign W = A;
endmodule

module Binary_Gray (
  input  A,
  input  B,
  input  C,
  input  D,
  output W,
  output X,
  output Y,
  output Z
);

  xor xor_1 (X, A, B);
  xor xor_2 (Y, B, C);
  xor xor_3 (Z, C, D);

  assign W = A;
endmodule

module BCD_Gray (
  input  A,
  input  B,
  input  C,
  input  D,
  output W,
  output X,
  output Y,
  output Z
);

  or or_1 (X, A, B);
  xor xor_1 (Y, B, C);
  xor xor_2 (Z, C, D);

  assign W = A;
endmodule

module Gray_BCD (
  input  A,
  input  B,
  input  C,
  input  D,
  output W,
  output X,
  output Y,
  output Z
);

  or or_1 (X, A, B);
  xor xor_1 (Y, X, C);
  xor xor_2 (Z, Y, D);

  assign W = A;
endmodule

module _4bitFull (
  input  Cin,
  input  A0,
  input  B0,
  input  A1,
  input  B1,
  input  A2,
  input  B2,
  input  A3,
  input  B3,
  output S0,
  output S1,
  output S2,
  output S3,
  output Cout
);

  wire fulladder_1_carry, fulladder_2_carry, fulladder_3_carry;

  FullAdder fulladder_1 (.A(Cin), .B(A0), .Cin(B0), .Sum(S0), .Carry(fulladder_1_carry));
  FullAdder fulladder_2 (.A(fulladder_1_carry), .B(A1), .Cin(B1), .Sum(S1), .Carry(fulladder_2_carry));
  FullAdder fulladder_3 (.A(fulladder_2_carry), .B(A2), .Cin(B2), .Sum(S2), .Carry(fulladder_3_carry));
  FullAdder fulladder_4 (.A(fulladder_3_carry), .B(A3), .Cin(B3), .Sum(S3), .Carry(Cout));
endmodule

module _4bitHalf (
  input  A0,
  input  A1,
  input  A2,
  input  A3,
  input  A4,
  output S0,
  output S1,
  output S2,
  output S3,
  output Cout
);

  wire halfadder_1_carry, halfadder_2_carry, halfadder_3_carry;

  HalfAdder halfadder_1 (.A(A0), .B(A1), .Sum(S0), .Carry(halfadder_1_carry));
  HalfAdder halfadder_2 (.A(halfadder_1_carry), .B(A2), .Sum(S1), .Carry(halfadder_2_carry));
  HalfAdder halfadder_3 (.A(halfadder_2_carry), .B(A3), .Sum(S2), .Carry(halfadder_3_carry));
  HalfAdder halfadder_4 (.A(halfadder_3_carry), .B(A4), .Sum(S3), .Carry(Cout));
endmodule

module HalfSubtractor (
  input  A,
  input  B,
  output Diff,
  output Borrow
);

  wire not_1_out;

  not not_1 (not_1_out, A);
  xor xor_1 (Diff, A, B);
  and A_prime_B (Borrow, not_1_out, B);

  // Notes on the sheet:
  //   A xor B
endmodule

module FullSubtractor (
  input  A,
  input  B,
  input  Bin,
  output Diff,
  output Borrow
);

  wire A_prime_B_out, and_1_out, not_1_out, xnor_1_out;

  not not_1 (not_1_out, A);
  ExactlyOne xor_1 (.out(Diff), .in0(A), .in1(B), .in2(Bin));
  and A_prime_B (A_prime_B_out, not_1_out, B);
  and and_1 (and_1_out, Bin, xnor_1_out);
  xnor xnor_1 (xnor_1_out, A, B);
  or or_1 (Borrow, A_prime_B_out, and_1_out);

  // Notes on the sheet:
  //   A xnor B
endmodule

// 8:1
module _8_1_MUX (
  input  S2,
  input  S1,
  input  S0,
  input  A0,
  input  A1,
  input  A2,
  input  A3,
  input  A4,
  input  A5,
  input  A6,
  input  A7,
  output out_12
);

  wire and_1_out, and_2_out, and_3_out, and_4_out, and_5_out, and_6_out, and_7_out, and_8_out, not_1_out,
       not_2_out, not_3_out;

  not not_1 (not_1_out, S2);
  not not_2 (not_2_out, S1);
  not not_3 (not_3_out, S0);
  and and_1 (and_1_out, not_3_out, not_2_out, not_1_out, A0);
  and and_2 (and_2_out, S0, not_2_out, not_1_out, A1);
  and and_3 (and_3_out, not_3_out, S1, not_1_out, A2);
  and and_4 (and_4_out, S0, S1, not_1_out, A3);
  and and_5 (and_5_out, not_3_out, not_2_out, S2, A4);
  and and_6 (and_6_out, S0, not_2_out, S2, A5);
  and and_7 (and_7_out, not_3_out, S1, S2, A6);
  and and_8 (and_8_out, S0, S1, S2, A7);
  or _8_1 (out_12, and_1_out, and_2_out, and_3_out, and_4_out, and_5_out, and_6_out, and_7_out, and_8_out);
endmodule

module _8_1_Mux_Sim (
  input  S2,
  input  S1,
  input  S0,
  input  A0,
  input  A1,
  input  A2,
  input  A3,
  input  A4,
  input  A5,
  input  A6,
  input  A7,
  input  A6_2,
  input  A6_3,
  output X
);

  _8_1_MUX u_8_1_mux_1 (
    .A0(A0), .A1(A1), .A2(A2), .A3(A3), .A4(A4), .A5(A5), .A6(A6), .A7(A7), .S2(S2), .S1(S1), .S0(S0),
    .out_12(X));
endmodule
